# Fritzing sketch arduino_cipi_motor (saved by Fritzing 0.9.1b)
circuit board: 8.46667cm x 5.64444cm
breadboards: 1

parts:
  Part1 = Arduino Uno (Rev3)
  J1 = double row female pin header, 10 pins [form="♀ (female)"]
  J2 = double row female pin header, 10 pins [form="♀ (female)"]
  J3 = female pin header, 3 pins [form="♀ (female)"]
  J4 = female pin header, 3 pins [form="♀ (female)"]

nets:
  N1: Part1.A1, J3.pin2
  N2: Part1.D8, J1.pin10
  N3: Part1.D9_PWM, J1.pin2
  N4: Part1.D10_PWM/SS, J1.pin9
  N5: Part1.D11_PWM/MOSI, J1.pin8
  N6: Part1.D12/MISO, J4.pin2
  N7: Part1.GND, J1.pin6, J1.pin7, J2.pin1, J3.pin3, J4.pin3
  N8: Part1.D2, J2.pin6
  N9: Part1.D3_PWM, J2.pin5
  N10: Part1.D4, J2.pin7
  N11: Part1.D5_PWM, J2.pin4
  N12: Part1.D6_PWM, J2.pin3
  N13: Part1.D7, J1.pin1
  N14: Part1.5V, J1.pin4, J1.pin5, J2.pin9, J2.pin10, J3.pin1, J4.pin1

notes:
  EMS30
